# Fritzing sketch power-supply-with-charger (saved by Fritzing 0.9.3b)
circuit board: 10cm x 5cm
breadboards: 2

parts:
  M1 = RioRand LM2596 [part_number="Power Supply 5 V"]
  M2 = RioRand LM2596 [part_number="Charger 8.4 V"]
  J1 = Screw terminal - 2 pins [part_number="Input 12 V" package=THT]
  J2 = Screw terminal - 2 pins [part_number="Output 5 V" package=THT]
  D2 = Schottky Diode [part_number=1N5817 package="300 mil [THT]"]
  VREG1 = Voltage Regulator - 5V [part_number="Voltage Regulator L4949V5" package="TO220 [THT]"]
  C1 = Capacitor [part_number="100 nF" package=cap-pth-small2]
  C2 = Capacitor Polarized [part_number="470 uF" package=panasonic_d]
  J4 = Screw terminal - 2 pins [part_number="Output 5 V" package=THT]
  D1 = Schottky Diode [part_number=1N5817 package="300 mil [THT]"]
  J5 = Screw terminal - 2 pins [part_number="Input 12 V" package=THT]
  F3 = Resettable Fuse PTC [part_number="Fuse 3A" package=ptc]
  J6 = Screw terminal - 2 pins [part_number="Battery 7.2 V" package=THT]

nets:
  N1: M1.Pin_1, M2.Pin_1, J1.pin1, VREG1.input_voltage, C1.2, D1.cathode, J5.pin1
  GND: M1.Pin_2, M1.Pin_4, M2.Pin_2, M2.Pin_4, J1.pin2, J2.pin2, VREG1.GND, C1.1, C2.-, J4.pin2, J5.pin2, J6.pin2
  N2: M1.Pin_3, J2.pin1, VREG1.output_voltage, C2.+, J4.pin1
  N3: M2.Pin_3, D2.anode
  N4: D2.cathode, D1.anode, F3.1
  N5: F3.2, J6.pin1
